# Fritzing sketch wodowskaz (saved by Fritzing 0.7.10b)
breadboards: 1

parts:
  Arduino1 = Arduino
  SPKR1 = Loudspeaker
  U1 = mystery part, 4 pins [chip_label=HC-SR04 spacing=300mil part_number=HC-SR04]
  DHT-1 = Humidity and Temperature Sensor DHT-22
  R1 = Resistor [tolerance=±5% resistance=220 package=THT]

nets:
  N1: Arduino1.GND, SPKR1.pin1, U1.pin4, DHT-1.GND_2
  N2: Arduino1.D10, U1.pin3
  N3: Arduino1.D9, U1.pin2
  N4: Arduino1.D3, SPKR1.pin2
  N5: Arduino1.D2, DHT-1.Data-signal, R1.Pin_0
  3V3: Arduino1.3V3, DHT-1.Vcc, R1.Pin_1
  N6: Arduino1.+5V, U1.pin1

custom parts:
  Humidity and Temperature Sensor DHT-22: Digital relative humidity & temperature sensor DHT-22
